// Logisim project CPU298.circ as structural Verilog: 23 circuits, main circuit PC-298
module PC_298 (
);

  wire Reset_out;
  wire [7:0] keyboard_1_data;
  wire [11:0] system_1_console_out;

  Button Reset (.out(Reset_out));
  System system_1 (.ResetIn(Reset_out), .Console_OUT(system_1_console_out), .Console_IN(keyboard_1_data));
  TTY #(.rows(25), .cols(80)) tty_1 (
    .data(system_1_console_out[6:0]), .clk(system_1_console_out[7]), .we(system_1_console_out[8]),
    .clr(system_1_console_out[9]));
  Keyboard keyboard_1 (
    .clk(system_1_console_out[7]), .re(system_1_console_out[10]), .clr(system_1_console_out[11]),
    .avail(keyboard_1_data[7]), .data(keyboard_1_data[6:0]));

  // Notes on the sheet:
  //   Key Input
endmodule

module System (
  input  ResetIn,
  input  [7:0] Console_IN,
  output [11:0] Console_OUT
);

  wire and_1_out, CLK, decoder_1_out0, decoder_1_out1, decoder_1_out2, decoder_1_out3, equal14_1_y,
       n2908c_core_1_read, n2908c_core_1_s0, n2908c_core_1_s1, n2908c_core_1_write, not_1_out, not_2_out,
       not_3_out, or_1_out, or_2_out;
  wire [6:0] n2908c_core_1_dataout;
  wire [7:0] register_1_q;
  wire [7:7] n2908c_core_1_dataout_2;
  wire [15:0] n2908c_core_1_addressout;

  Clock Clock (.out(CLK));
  _2908C_CORE u_2908c_core_1 (
    .Reset(ResetIn), .DataOut({n2908c_core_1_dataout_2[7], n2908c_core_1_dataout}),
    .DataIn({n2908c_core_1_dataout_2[7], n2908c_core_1_dataout}), .Read(n2908c_core_1_read),
    .AddressOut(n2908c_core_1_addressout), .CLK(CLK), .Write(n2908c_core_1_write), .S0(n2908c_core_1_s0),
    .S1(n2908c_core_1_s1));
  // Probe on n2908c_core_1_addressout
  // Probe on {n2908c_core_1_dataout_2[7], n2908c_core_1_dataout}
  not not_1 (not_1_out, n2908c_core_1_write);
  or or_1 (or_1_out, n2908c_core_1_read, n2908c_core_1_write);
  Pull_Resistor pull_resistor_1 (.node({n2908c_core_1_dataout_2[7], n2908c_core_1_dataout}));
  Pull_Resistor pull_resistor_2 (.node(n2908c_core_1_addressout));
  and and_1 (and_1_out, or_1_out, not_2_out);
  Decoder #(.select(2), .disabled(0)) decoder_1 (
    .out0(decoder_1_out0), .out1(decoder_1_out1), .out2(decoder_1_out2), .out3(decoder_1_out3),
    .sel(n2908c_core_1_addressout[15:14]), .en(and_1_out));
  not not_2 (not_2_out, equal14_1_y);
  Equal14 equal14_1 (.In0(n2908c_core_1_addressout[15:2]), .In1(14'h3f84), .Y(equal14_1_y));
  and and_2 (Console_OUT[8], equal14_1_y, not_1_out);
  and and_3 (Console_OUT[10], equal14_1_y, n2908c_core_1_read);
  assign {n2908c_core_1_dataout_2[7], n2908c_core_1_dataout} = Console_OUT[10] ? register_1_q : 8'bz;  // Controlled_Buffer controlled_buffer_1
  ROM #(.addrWidth(14)) rom_1 (
    .addr(n2908c_core_1_addressout[13:0]), .data({n2908c_core_1_dataout_2[7], n2908c_core_1_dataout}),
    .sel(decoder_1_out0));
  assign Console_OUT[6:0] = Console_OUT[8] ? n2908c_core_1_dataout : 7'bz;  // Controlled_Buffer controlled_buffer_2
  or or_2 (or_2_out, Console_OUT[8], Console_OUT[10]);
  not not_3 (not_3_out, or_2_out);
  not not_4 (Console_OUT[7], not_3_out);
  RAM #(.addrWidth(14)) ram_1 (
    .addr(n2908c_core_1_addressout[13:0]), .data({n2908c_core_1_dataout_2[7], n2908c_core_1_dataout}),
    .sel(decoder_1_out1), .clk(not_1_out), .ld(n2908c_core_1_read), .clr(1'b0));
  Register register_1 (.D(Console_IN), .en(Console_OUT[10]), .Q(register_1_q), .clk(Console_OUT[10]), .clr(ResetIn));
  RAM #(.addrWidth(14)) ram_2 (
    .addr(n2908c_core_1_addressout[13:0]), .data({n2908c_core_1_dataout_2[7], n2908c_core_1_dataout}),
    .sel(decoder_1_out2), .clk(not_1_out), .ld(n2908c_core_1_read), .clr(1'b0));
  RAM #(.addrWidth(14)) ram_3 (
    .addr(n2908c_core_1_addressout[13:0]), .data({n2908c_core_1_dataout_2[7], n2908c_core_1_dataout}),
    .sel(decoder_1_out3), .clk(not_1_out), .ld(n2908c_core_1_read), .clr(1'b0));

  assign {Console_OUT[11], Console_OUT[9]} = {2{ResetIn}};

  // Other names for the same wires on the sheet: Reset = ResetIn

  // Notes on the sheet:
  //   ROM0
  //   RAM0
  //   contents of rom_1 (hex, n*v repeats v):
  //   8 5a 28 0 80 2 ee fe 5 bf e5 4 d7 fe 2 0 ee fe 7c 0 f 0 a5 8 e5 fb d6 9 fe e9 ff 48 65 6c 6c 6f 0 6e
  //   48 65 6c 6c 6f 43*0 76 1199*0 76 2553*0 f8 aa 8478*0 6e
  //   RAM1
  //   RAM2
endmodule

module Equal14 (
  input  [13:0] In0,
  input  [13:0] In1,
  output Y
);

  wire [13:0] not_1_out, xor_1_out;

  assign not_1_out = ~xor_1_out;  // NOT_Gate not_1, 14 bits wide
  assign xor_1_out = In0 ^ In1;  // XOR_Gate xor_1, 14 bits wide
  and and_1 (Y, not_1_out[0], not_1_out[1], not_1_out[2], not_1_out[3], not_1_out[4], not_1_out[5], not_1_out[6], not_1_out[7], not_1_out[8], not_1_out[9], not_1_out[10], not_1_out[11], not_1_out[12], not_1_out[13]);
endmodule

module _2908C_CORE (
  input  [7:0] DataIn,
  input  CLK,
  input  Reset,
  output [7:0] DataOut,
  output [15:0] AddressOut,
  output Write,
  output S0,
  output Read,
  output S1
);

  wire and_1_out, and_2_out, and_3_out, and_4_out, clk_gen_1_wait, d_ff_1_qn, d_ff_2_qn, E, nRST, or_1_out,
       Q, sequencer_1_jump_op, sequencer_1_ndo_jump, \sequencer_1_set_μrom_address , sequencer_1_stateclock,
       sequencer_1_stepctrl, sequencer_1_stepupdate, undriven;
  wire [1:0] sequencer_1_exbuscontrol;
  wire [2:0] executer_1_flagregisterout;
  wire [5:0] sequencer_1_aluop;
  wire [7:0] executer_1_dataout, sequencer_1_dataout, sequencer_1_executercontrol;
  wire [11:0] sequencer_1_step;
  wire [15:0] executer_1_addrout;

  CLK_GEN clk_gen_1 (.nMRDY(undriven), .CLK(CLK), .Reset(Reset), .Q(Q), .E(E), .WAIT(clk_gen_1_wait), .nRST(nRST));
  Executer executer_1 (
    .DataOut(executer_1_dataout), .FlagRegisterOut(executer_1_flagregisterout), .E(E),
    .AddrOut(executer_1_addrout), .DataIn(sequencer_1_dataout), .RegisterCtrl(sequencer_1_executercontrol),
    .STEP(sequencer_1_step), .ALUOP(sequencer_1_aluop), .Q(Q));
  // Probe on sequencer_1_executercontrol
  // Probe on sequencer_1_aluop
  Sequencer sequencer_1 (
    .FlagIn(executer_1_flagregisterout), .Q(Q), .E(E), .nReset(nRST), .DataIn(DataIn),
    .ExecuterControl(sequencer_1_executercontrol), .ExBusControl(sequencer_1_exbuscontrol),
    .STEP(sequencer_1_step), .DataOut(sequencer_1_dataout), .S1(S1), .S0(S0),
    .StepUpdate(sequencer_1_stepupdate), .JUMP_OP(sequencer_1_jump_op), .nDO_JUMP(sequencer_1_ndo_jump),
    .StateClock(sequencer_1_stateclock), .StepCtrl(sequencer_1_stepctrl),
    .\Set_μROM_Address (\sequencer_1_set_μrom_address ), .ALUOP(sequencer_1_aluop));
  D_Latch16 d_latch16_1 (.In(executer_1_addrout), .Out(AddressOut), .LE(or_1_out), .CLK_Q(Q));
  D_Latch8 d_latch8_1 (.In(executer_1_dataout), .LE(or_1_out), .OE(and_1_out), .Out(DataOut), .CLK_Q(Q));
  or or_1 (or_1_out, E, Q);
  and and_1 (and_1_out, or_1_out, and_3_out);
  and and_2 (and_2_out, E, ~Q);  // AND_Gate
  and and_3 (and_3_out, ~sequencer_1_exbuscontrol[0], sequencer_1_exbuscontrol[1]);  // AND_Gate
  and and_4 (and_4_out, sequencer_1_exbuscontrol[0], ~sequencer_1_exbuscontrol[1]);  // AND_Gate
  D_Flip_Flop d_ff_1 (.clk(Q), .D(and_3_out), .Qn(d_ff_1_qn), .reset(and_2_out));  // open: Q, preset, en
  not not_1 (Write, d_ff_1_qn);
  D_Flip_Flop d_ff_2 (.clk(Q), .D(and_4_out), .Qn(d_ff_2_qn), .reset(and_2_out));  // open: Q, preset, en
  not not_2 (Read, d_ff_2_qn);

  // Notes on the sheet:
  //   Reset: pull=up
  //   トランスペアレントラッチ
  //   Q or E がラッチイネーブル
  //   573
  //   DataBus_In
  //   DataBus_Out
  //   AddressBus
  //   Q↓からE↓までの間クリア
endmodule

module Sequencer (
  input  [7:0] DataIn,
  input  nReset,
  input  Q,
  input  E,
  input  [2:0] FlagIn,
  output [11:0] STEP,
  output \Set_μROM_Address ,
  output [7:0] ExecuterControl,
  output StepCtrl,
  output StepUpdate,
  output [5:0] ALUOP,
  output [1:0] ExBusControl,
  output StateClock,
  output [7:0] DataOut,
  output JUMP_OP,
  output S1,
  output S0,
  output nDO_JUMP
);

  wire and_1_out, and_2_out, and_3_out, and_5_out, and_7_out, and_8_out, Bit0_qn, Bit1_qn, d_ff_1_q,
       multiplexer_3_out, multiplexer_4_out, nE, nor_1_out, not_3_out, not_4_out, not_5_out, not_6_out,
       not_7_out, not_8_out, not_9_out, not_10_out, not_11_out, not_12_out, not_13_out, not_14_out, nQ,
       or_2_out, step0;
  wire [3:0] multiplexer_1_out;
  wire [7:0] IR_q, multiplexer_2_out;
  wire [15:0] urom_a_1_ctrlsignal;

  not not_1 (nQ, Q);
  not not_2 (nE, E);
  // Probe on {DataIn[7:4], multiplexer_1_out}
  Multiplexer #(.width(4), .disabled(0), .enable("false")) multiplexer_1 (
    .in0(DataIn[3:0]), .in1({3'b111, nDO_JUMP}), .out(multiplexer_1_out), .sel(JUMP_OP));
  D_Flip_Flop d_ff_1 (.clk(Q), .D(and_1_out), .Q(d_ff_1_q), .reset(not_3_out));  // open: Qn, preset, en
  not not_3 (not_3_out, nReset);
  and and_1 (and_1_out, step0, and_2_out);
  Register IR (.D({DataIn[7:4], multiplexer_1_out}), .en(d_ff_1_q), .Q(IR_q), .clk(E));  // open: clr
  and and_2 (and_2_out, S0, Bit1_qn);
  not not_4 (not_4_out, nReset);
  Multiplexer #(.width(8), .disabled(0), .enable("false")) multiplexer_2 (
    .in0(IR_q), .in1({6'b111000, S1, S0}), .out(multiplexer_2_out), .sel(not_5_out));
  not not_5 (not_5_out, and_3_out);
  and and_3 (and_3_out, S1, Bit0_qn);
  D_Flip_Flop Bit1 (.clk(StateClock), .D(and_2_out), .Q(S1), .Qn(Bit1_qn), .reset(not_4_out));  // open: preset, en
  D_Flip_Flop Bit0 (.clk(StateClock), .D(Bit0_qn), .Q(S0), .Qn(Bit0_qn), .reset(not_4_out));  // open: preset, en
  D_Flip_Flop StepControl (.clk(Q), .D(not_6_out), .Qn(StepCtrl), .reset(not_7_out));  // open: Q, preset, en
  not not_6 (not_6_out, StepUpdate);
  not not_7 (not_7_out, nReset);
  // Probe on multiplexer_2_out
  D_Flip_Flop Stage_Control (.clk(nE), .D(StepUpdate), .Qn(StateClock), .reset(not_8_out));  // open: Q, preset, en
  not not_8 (not_8_out, and_5_out);
  or or_1 (\Set_μROM_Address , E, and_5_out);
  // Probe on STEP
  uROM_A urom_a_1 (
    .OpeCode(multiplexer_2_out), .Load(StepCtrl), .Update(\Set_μROM_Address ), .STEP_MON(STEP),
    .CtrlSignal(urom_a_1_ctrlsignal));
  and and_4 (StepUpdate, urom_a_1_ctrlsignal[14], urom_a_1_ctrlsignal[15], nQ);
  and and_5 (and_5_out, nReset, nQ);
  nor nor_1 (nor_1_out, FlagIn[0], FlagIn[1]);
  or or_2 (or_2_out, FlagIn[0], FlagIn[1]);
  not not_9 (not_9_out, FlagIn[2]);
  // Probe on urom_a_1_ctrlsignal
  Multiplexer #(.select(2), .disabled(0), .enable("false")) multiplexer_3 (
    .in0(nor_1_out), .in1(or_2_out), .in2(FlagIn[2]), .in3(not_9_out), .out(multiplexer_3_out),
    .sel(DataIn[1:0]));
  not not_10 (not_10_out, FlagIn[0]);
  not not_11 (not_11_out, FlagIn[1]);
  nor nor_2 (step0, STEP[0], STEP[1]);
  and and_6 (JUMP_OP, ~DataIn[3], ~DataIn[4], DataIn[5], DataIn[6], DataIn[7]);  // AND_Gate
  Multiplexer #(.select(2), .disabled(0), .enable("false")) multiplexer_4 (
    .in0(not_10_out), .in1(FlagIn[0]), .in2(not_11_out), .in3(FlagIn[1]), .out(multiplexer_4_out),
    .sel(DataIn[1:0]));
  Register Ctrl_signal_register_LO (
    .D(urom_a_1_ctrlsignal[7:0]), .Q(ExecuterControl), .clk(nE), .clr(not_12_out));  // open: en
  not not_12 (not_12_out, nReset);
  Register Ctrl_signal_register_HI (
    .D(urom_a_1_ctrlsignal[15:8]), .Q({ExBusControl, ALUOP}), .clk(nE), .clr(not_13_out));  // open: en
  not not_13 (not_13_out, nReset);
  and and_7 (and_7_out, DataIn[2], multiplexer_3_out);
  not not_14 (not_14_out, DataIn[2]);
  and and_8 (and_8_out, not_14_out, multiplexer_4_out);
  nor nor_3 (nDO_JUMP, and_7_out, and_8_out);

  assign DataOut = DataIn;

  // Other names for the same wires on the sheet: DO_JUMP = nDO_JUMP; CY = FlagIn[0]; ZF = FlagIn[1]; SF = FlagIn[2]

  // Notes on the sheet:
  //   nReset: pull=up
  //   実行ステート以外のときは0xEXにする
  //   μROM_IDX
  //   通常E↑で変化する
  //   HCT
endmodule

module Executer (
  input  Q,
  input  E,
  input  [11:0] STEP,
  input  [7:0] DataIn,
  input  [5:0] ALUOP,
  input  [7:0] RegisterCtrl,
  output [2:0] FlagRegisterOut,
  output [7:0] DataOut,
  output [15:0] AddrOut
);

  wire and_1_out, decoder_1_out1, decoder_1_out2, decoder_1_out3, decoder_1_out4, decoder_1_out5,
       decoder_1_out6, decoder_1_out7, op_1_fl;
  wire [1:0] alu8c_1_carry_2;
  wire [3:0] op_1_op;
  wire [7:0] A_q, alu8c_1_loutmon, H_q, L_q, multiplexer_1_out, mux4to1x8_1_y, mux4to1x16_1_y,
       mux4to1x16_1_y_2, op_1_opout, W_q;
  wire [15:0] PC_q, X_q, Y_q;

  // Probe on STEP
  // Probe on DataIn
  Decoder #(.select(3), .disabled(0), .enable("false")) decoder_1 (
    .out1(decoder_1_out1), .out2(decoder_1_out2), .out3(decoder_1_out3), .out4(decoder_1_out4),
    .out5(decoder_1_out5), .out6(decoder_1_out6), .out7(decoder_1_out7), .sel(RegisterCtrl[7:5]));  // open: out0
  Register A (.D(DataOut), .en(decoder_1_out1), .Q(A_q), .clk(E));  // open: clr
  Register W (.D(DataOut), .en(decoder_1_out2), .Q(W_q), .clk(E));  // open: clr
  Register H (.D(DataOut), .en(decoder_1_out3), .Q(H_q), .clk(E));  // open: clr
  Register L (.D(DataOut), .en(decoder_1_out4), .Q(L_q), .clk(E));  // open: clr
  Register #(.width(16)) X (.D(AddrOut), .en(decoder_1_out5), .Q(X_q), .clk(E));  // open: clr
  Register #(.width(16)) Y (.D(AddrOut), .en(decoder_1_out6), .Q(Y_q), .clk(E));  // open: clr
  Register #(.width(16)) PC (.D(AddrOut), .en(decoder_1_out7), .Q(PC_q), .clk(E));  // open: clr
  // Probe on AddrOut
  Multiplexer #(.width(8), .enable("false")) multiplexer_1 (
    .in0(A_q), .in1(W_q), .out(multiplexer_1_out), .sel(RegisterCtrl[2]));
  MUX4to1x16 mux4to1x16_1 (
    .D0({H_q, L_q}), .D1(X_q), .D2(Y_q), .D3(PC_q), .Sel(RegisterCtrl[4:3]),
    .Y({mux4to1x16_1_y_2, mux4to1x16_1_y}));  // open: I0, I1, I2, I3
  MUX4to1x8 mux4to1x8_1 (
    .D0(DataIn), .D1(W_q), .D2(mux4to1x16_1_y_2), .D3(mux4to1x16_1_y), .Sel(RegisterCtrl[1:0]),
    .Y(mux4to1x8_1_y));  // open: I0, I1, I2, I3
  // Probe on {mux4to1x16_1_y_2, mux4to1x16_1_y}
  // Probe on op_1_op
  // Probe on mux4to1x8_1_y
  OP op_1 (.OPin(ALUOP[3:0]), .OP(op_1_op), .OpOut(op_1_opout), .FL(op_1_fl));
  INC_DEC16 inc_dec16_1 (.IN({mux4to1x16_1_y_2, mux4to1x16_1_y}), .OUT(AddrOut), .INC_DEC(ALUOP[5]), .CI(ALUOP[4]));
  // Probe on alu8c_1_loutmon
  ALU8C alu8c_1 (
    .A(multiplexer_1_out), .Carry_2(alu8c_1_carry_2[0]), .ALU_OUT(DataOut), .ZF(alu8c_1_carry_2[1]),
    .B(mux4to1x8_1_y), .LOutMon(alu8c_1_loutmon), .OpIn(op_1_opout), .Carry(FlagRegisterOut[0]));
  Register #(.width(3)) Flag (
    .D({DataOut[7], alu8c_1_carry_2}), .en(op_1_fl), .Q(FlagRegisterOut), .clk(E));  // open: clr
  and and_1 (and_1_out, ~ALUOP[4], ALUOP[5]);  // AND_Gate

  // Other names for the same wires on the sheet: ALUOP_t[3:0] = ALUOP[3:0]; ADDR[1:0] = ALUOP[5:4];
  //   CarryFlag = FlagRegisterOut[0]; ALU_B[1:0] = RegisterCtrl[1:0]; Acc = RegisterCtrl[2];
  //   WRSel[1:0] = RegisterCtrl[4:3]; WriteBackSel[2:0] = RegisterCtrl[7:5]

  // Notes on the sheet:
  //   Writeback
  //   Selector
  //   238
  //   139
endmodule

module D_Latch16 (
  input  [15:0] In,
  input  CLK_Q,
  input  LE,
  output [15:0] Out
);

  wire [7:0] register_1_q, register_2_q;

  Register register_1 (.D(In[7:0]), .Q(register_1_q), .clk(CLK_Q));  // open: en, clr
  Register register_2 (.D(In[15:8]), .Q(register_2_q), .clk(CLK_Q));  // open: en, clr
  Multiplexer #(.width(16), .disabled(0), .enable("false")) multiplexer_1 (
    .in0(In), .in1({register_2_q, register_1_q}), .out(Out), .sel(LE));
endmodule

module D_Latch8 (
  input  [7:0] In,
  input  CLK_Q,
  input  LE,
  input  OE,
  output [7:0] Out
);

  wire [7:0] multiplexer_1_out, register_1_q;

  Register register_1 (.D(In), .Q(register_1_q), .clk(CLK_Q));  // open: en, clr
  Multiplexer #(.width(8), .disabled(0), .enable("false")) multiplexer_1 (
    .in0(In), .in1(register_1_q), .out(multiplexer_1_out), .sel(LE));
  assign Out = OE ? multiplexer_1_out : 8'bz;  // Controlled_Buffer controlled_buffer_1
endmodule

module CLK_GEN (
  input  nMRDY,
  input  CLK,
  input  Reset,
  output Q,
  output E,
  output WAIT,
  output nRST
);

  wire and_1_out, d_ff_1_q, d_ff_1_qn, d_ff_2_q, d_ff_3_q, d_ff_4_q, d_ff_5_qn, nand_1_out, nor_1_out,
       not_1_out, not_2_out, not_3_out, not_4_out, not_5_out, not_6_out, not_7_out, not_8_out, not_9_out,
       PowerOnReset_q;

  not not_1 (not_1_out, nMRDY);
  Pull_Resistor pull_resistor_1 ();  // open: node
  not not_2 (not_2_out, CLK);
  not not_3 (not_3_out, Reset);
  D_Flip_Flop d_ff_1 (.clk(not_2_out), .D(1'b0), .Q(d_ff_1_q), .Qn(d_ff_1_qn), .preset(not_4_out));  // open: en, reset
  not not_4 (not_4_out, and_1_out);
  D_Flip_Flop PowerOnReset (.clk(not_2_out), .D(1'b1), .Q(PowerOnReset_q));  // open: Qn, preset, en, reset
  nand nand_1 (nand_1_out, ~Q, not_1_out, E);  // NAND_Gate
  D_Flip_Flop d_ff_2 (.clk(not_2_out), .D(d_ff_1_q), .Q(d_ff_2_q), .preset(not_5_out));  // open: Qn, en, reset
  not not_5 (not_5_out, and_1_out);
  not not_6 (not_6_out, and_1_out);
  and and_1 (and_1_out, not_3_out, PowerOnReset_q);
  D_Flip_Flop d_ff_3 (.clk(not_2_out), .D(nand_1_out), .Q(d_ff_3_q), .preset(d_ff_4_q));  // open: Qn, en, reset
  not not_7 (not_7_out, not_2_out);
  D_Flip_Flop d_ff_4 (.clk(not_2_out), .D(d_ff_2_q), .Q(d_ff_4_q), .preset(not_6_out));  // open: Qn, en, reset
  nor nor_1 (nor_1_out, d_ff_4_q, ~d_ff_3_q);  // NOR_Gate
  D_Flip_Flop d_ff_5 (.clk(not_7_out), .D(Q), .Q(E), .Qn(d_ff_5_qn), .preset(not_8_out));  // open: en, reset
  not not_8 (not_8_out, d_ff_3_q);
  D_Flip_Flop d_ff_6 (.clk(not_7_out), .D(d_ff_5_qn), .Q(Q), .reset(not_9_out));  // open: Qn, preset, en
  not not_9 (not_9_out, nor_1_out);
  not not_10 (WAIT, d_ff_3_q);
  not not_11 (nRST, d_ff_4_q);

  // Notes on the sheet:
  //   LogiSimのシミュレーションリセット対応
endmodule

module INC_DEC16 (
  input  CI,
  input  INC_DEC,
  input  [15:0] IN,
  output [15:0] OUT
);

  wire inc_dec8_1_cout;

  INC_DEC8 inc_dec8_1 (.nThru(CI), .INC_DEC(INC_DEC), .CI(CI), .A(IN[7:0]), .Y(OUT[7:0]), .COut(inc_dec8_1_cout));
  INC_DEC8 inc_dec8_2 (.nThru(CI), .INC_DEC(INC_DEC), .CI(inc_dec8_1_cout), .A(IN[15:8]), .Y(OUT[15:8]));  // open: COut
endmodule

module INC_DEC8 (
  input  nThru,
  input  INC_DEC,
  input  CI,
  input  [7:0] A,
  output [7:0] Y,
  output COut
);

  wire and_1_out, and_2_out, and_3_out, and_4_out, and_5_out, and_6_out, and_7_out, and_8_out, and_9_out,
       and_10_out, and_11_out, and_12_out, and_13_out, and_14_out, and_15_out, and_16_out, multiplexer_1_out,
       multiplexer_2_out, multiplexer_3_out, multiplexer_4_out, multiplexer_5_out, multiplexer_6_out,
       multiplexer_7_out, nDEC, Thru;
  wire [7:0] xor_1_out;

  not not_1 (Thru, nThru);
  not not_2 (nDEC, INC_DEC);
  and and_1 (and_1_out, CI, A[0]);
  and and_2 (and_2_out, CI, ~A[0]);  // AND_Gate
  and and_3 (and_3_out, and_1_out, A[1]);
  and and_4 (and_4_out, and_2_out, ~A[1]);  // AND_Gate
  and and_5 (and_5_out, and_3_out, A[2]);
  and and_6 (and_6_out, and_4_out, ~A[2]);  // AND_Gate
  and and_7 (and_7_out, and_5_out, A[3]);
  and and_8 (and_8_out, and_6_out, ~A[3]);  // AND_Gate
  and and_9 (and_9_out, and_7_out, A[4]);
  and and_10 (and_10_out, and_8_out, ~A[4]);  // AND_Gate
  and and_11 (and_11_out, and_9_out, A[5]);
  and and_12 (and_12_out, and_10_out, ~A[5]);  // AND_Gate
  and and_13 (and_13_out, and_11_out, A[6]);
  and and_14 (and_14_out, and_12_out, ~A[6]);  // AND_Gate
  and and_15 (and_15_out, and_13_out, A[7]);
  and and_16 (and_16_out, and_14_out, ~A[7]);  // AND_Gate
  Multiplexer #(.disabled(0), .enable("false")) multiplexer_1 (
    .in0(and_1_out), .in1(and_2_out), .out(multiplexer_1_out), .sel(INC_DEC));
  Multiplexer #(.disabled(0), .enable("false")) multiplexer_2 (
    .in0(and_3_out), .in1(and_4_out), .out(multiplexer_2_out), .sel(INC_DEC));
  Multiplexer #(.disabled(0), .enable("false")) multiplexer_3 (
    .in0(and_5_out), .in1(and_6_out), .out(multiplexer_3_out), .sel(INC_DEC));
  Multiplexer #(.disabled(0), .enable("false")) multiplexer_4 (
    .in0(and_7_out), .in1(and_8_out), .out(multiplexer_4_out), .sel(INC_DEC));
  Multiplexer #(.disabled(0), .enable("false")) multiplexer_5 (
    .in0(and_9_out), .in1(and_10_out), .out(multiplexer_5_out), .sel(INC_DEC));
  Multiplexer #(.disabled(0), .enable("false")) multiplexer_6 (
    .in0(and_11_out), .in1(and_12_out), .out(multiplexer_6_out), .sel(INC_DEC));
  Multiplexer #(.disabled(0), .enable("false")) multiplexer_7 (
    .in0(and_13_out), .in1(and_14_out), .out(multiplexer_7_out), .sel(INC_DEC));
  Multiplexer #(.disabled(0), .enable("false")) multiplexer_8 (
    .in0(and_15_out), .in1(and_16_out), .out(COut), .sel(INC_DEC));
  xor xor_1 (xor_1_out[0], CI, A[0]);
  xor xor_2 (xor_1_out[1], multiplexer_1_out, A[1]);
  xor xor_3 (xor_1_out[2], multiplexer_2_out, A[2]);
  xor xor_4 (xor_1_out[3], multiplexer_3_out, A[3]);
  xor xor_5 (xor_1_out[4], multiplexer_4_out, A[4]);
  xor xor_6 (xor_1_out[5], multiplexer_5_out, A[5]);
  xor xor_7 (xor_1_out[6], multiplexer_6_out, A[6]);
  xor xor_8 (xor_1_out[7], multiplexer_7_out, A[7]);
  Multiplexer #(.width(8), .disabled(0), .enable("false")) multiplexer_9 (
    .in0(xor_1_out), .in1(A), .out(Y), .sel(Thru));

  // Other names for the same wires on the sheet: DEC = INC_DEC
endmodule

module uROM_A (
  input  [7:0] OpeCode,
  input  Load,
  input  Update,
  output [11:0] STEP_MON,
  output [15:0] CtrlSignal
);

  wire not_1_out;

  not not_1 (not_1_out, Load);
  Counter #(.width(4), .max('hf)) _161 (
    .load(Load), .D(4'b0000), .count(not_1_out), .Q(STEP_MON[3:0]), .clk(Update));  // open: carry, clr
  Register _377 (.D(OpeCode), .en(Load), .Q(STEP_MON[11:4]), .clk(Update));  // open: clr
  // Probe on STEP_MON
  ROM #(.addrWidth(12), .dataWidth(16)) rom_1 (.addr(STEP_MON), .data(CtrlSignal));  // open: sel

  // Notes on the sheet:
  //   contents of rom_1 (hex, n*v repeats v):
  //   c000 31*0 8808 c009 94*0 4938 d0f8 94*0 4958 10f8 a8f 94a e6e c928 410*0 4998 10f8 4978 10f8 c0a0
  //   379*0 c92b 527*0 4998 10f8 4978 10f8 c0c0 2028*0 80 60 c0e0 12*0 4018 d0f8 206*0 4958 10f8 a9f 744
  //   c7e c0e0 10*0 d0f8
endmodule

module uROM_A_8 (
  input  [7:0] OpeCode,
  input  Load,
  input  Update,
  output [12:0] STEP_MON,
  output [7:0] CtrlSignal
);

  wire not_1_out;

  not not_1 (not_1_out, Load);
  Counter #(.width(5), .max('h1f)) counter_1 (
    .load(Load), .D({5{1'b0}}), .count(not_1_out), .Q(STEP_MON[4:0]), .clk(Update));  // open: carry, clr
  Register _377 (.D(OpeCode), .en(Load), .Q(STEP_MON[12:5]), .clk(Update));  // open: clr
  // Probe on STEP_MON
  ROM #(.addrWidth(13)) rom_1 (.addr(STEP_MON), .data(CtrlSignal));  // open: sel

  // Notes on the sheet:
  //   contents of rom_1 (hex, n*v repeats v):
  //   c 0 c 0 c 0 c 0 c 0 c 0 c 0 c 0 c 0 8c 0 c 0 8c 0 c 0 8c 0 c 0 8c 0 c 1c c 1c c 1c c 1c c 1c c 1c c
  //   1c c 1c c 1c c 1c c 1c c 1c c 1c c 1c c 1c c 1c c 1c c 1c c 1c c 1c c 0 1c 0 c 0 c 0 1c 0 c 0 c 1c c
  //   1c c 1c c 1c c 0 c 0 c 0 c 18*0 80 0 80 0 80 0 80 80 0 80 0 4*c 0 80 0 80 0 80 0 80 0 0 80 0 20 80 0
  //   20 0 80 0 80 0 80 0 80 4*0 8 8 0 0 80 8 8 8 c 1c c c 1c c c 4*15 c 1c c 1c c 1c c 1c 10*0 80 c 0 0
  //   80 0 c 0 1c c 0 1c c 0 c 0 c 1c c 1c c 1c c 1c 4*0 80 33 33 0 80 33 33 80 b3 33 4*0 80 e e 0 80 e e
  //   80 8e e 4*0 80 30 30 0 80 30 30 80 b0 30 4*0 80 c c 0 80 c c 80 8c c 4*0 80 60 60 0 80 60 60 80 e0
  //   60 4*0 80 e e 0 80 e e 80 8e e 4*0 80 58 58 0 80 58 58 80 d8 58 4*0 80 78 78 0 80 78 78 80 f8 78 0
  //   80 70 0 70 80 70 0 80 28 0 28 80 28 0 80 34 0 34 80 34 0 80 35 0 35 80 35 2 82 2 82 2 80 2 1c 1c 3f
  //   bf 3f bf 3f bc 3f 8 8 0 c 1c 12*0 8 c 1c c 1c 1c 7*0 80 f8 0 80 d8 8 8 c 1c 0 0 c 1c c 1c
endmodule

module ALU8C (
  input  [7:0] A,
  input  [7:0] B,
  input  Carry,
  input  [7:0] OpIn,
  output [7:0] LOutMon,
  output ZF,
  output [7:0] ALU_OUT,
  output Carry_2
);

  wire alu8a_1_cy, multiplexer_1_out, multiplexer_3_out, xor_1_out;
  wire [7:0] alu8a_1_y, alu_1_y;

  ALU alu_1 (.A(A), .B(B), .S(OpIn[3:0]), .Y(alu_1_y));
  // Probe on OpIn[3:0]
  SignEx signex_1 (.A(alu_1_y), .Y(LOutMon), .Thru(OpIn[7]));
  Multiplexer #(.disabled(0), .enable("false")) multiplexer_1 (
    .in0(1'b0), .in1(Carry), .out(multiplexer_1_out), .sel(OpIn[6]));
  xor xor_1 (xor_1_out, multiplexer_1_out, OpIn[5]);
  ALU8A alu8a_1 (.B(LOutMon), .A(A), .Cin(xor_1_out), .CY(alu8a_1_cy), .Y(alu8a_1_y));
  Multiplexer #(.width(8), .disabled(0), .enable("false")) multiplexer_2 (
    .in0(alu8a_1_y), .in1(LOutMon), .out(ALU_OUT), .sel(OpIn[4]));
  Multiplexer #(.disabled(0), .enable("false")) multiplexer_3 (
    .in0(alu8a_1_cy), .in1(1'b0), .out(multiplexer_3_out), .sel(OpIn[4]));
  ZeroFlag zeroflag_1 (.A(ALU_OUT), .Y(ZF));
  xor xor_2 (Carry_2, multiplexer_3_out, OpIn[5]);

  // Notes on the sheet:
  //   4078
endmodule

module OP (
  input  [3:0] OPin,
  output [7:0] OpOut,
  output [3:0] OP,
  output FL
);

  wire optable_1_fl;

  OpTable optable_1 (
    .A2(OPin[3]), .A1(OPin[2]), .A0(OPin[1]), .D3(OP[3]), .M(OPin[0]), .D2(OP[2]), .D1(OP[1]), .D0(OP[0]),
    .MO(OpOut[4]), .FL(optable_1_fl), .CInv(OpOut[5]));  // open: Ci
  not not_1 (FL, optable_1_fl);
  and and_1 (OpOut[7], ~OPin[3], OPin[2], OPin[1], OPin[0]);  // AND_Gate

  assign {OpOut[6], OpOut[3:0]} = {OPin[2], OP};
endmodule

module OpTable (
  input  A2,
  input  A1,
  input  A0,
  input  M,
  output D3,
  output D2,
  output D1,
  output D0,
  output MO,
  output Ci,
  output FL,
  output CInv
);

  wire and_1_out, and_2_out, and_3_out, and_4_out, and_5_out, and_6_out, and_7_out, and_8_out, and_9_out,
       and_10_out, and_11_out, and_12_out, and_13_out, and_14_out, and_15_out, and_16_out, and_17_out,
       and_18_out, and_19_out, and_20_out, and_21_out, and_22_out, and_23_out, and_24_out, and_25_out,
       and_26_out, and_27_out, and_28_out, and_29_out, and_30_out, not_1_out, not_2_out, not_3_out,
       not_4_out, not_5_out, not_6_out, not_7_out, not_8_out, not_9_out, not_10_out, not_11_out, not_12_out,
       not_13_out, not_14_out, not_15_out, not_16_out, not_17_out, not_18_out, not_19_out, not_20_out,
       not_21_out, not_22_out, not_23_out, not_24_out, not_25_out, not_26_out, not_27_out, not_28_out,
       not_29_out, not_30_out, not_31_out, not_32_out, not_33_out, not_34_out, not_35_out, not_36_out,
       not_37_out, not_38_out, not_39_out, not_40_out;

  not not_1 (not_1_out, A1);
  and and_1 (and_1_out, not_1_out, not_2_out, M);
  not not_2 (not_2_out, A0);
  not not_3 (not_3_out, A2);
  and and_2 (and_2_out, not_3_out, A0, not_4_out);
  not not_4 (not_4_out, M);
  and and_3 (and_3_out, A1, A0, M);
  and and_4 (and_4_out, A2, not_5_out, not_6_out);
  not not_5 (not_5_out, A1);
  not not_6 (not_6_out, M);
  and and_5 (and_5_out, A2, not_7_out, not_8_out);
  not not_7 (not_7_out, A0);
  not not_8 (not_8_out, M);
  not not_9 (not_9_out, A2);
  not not_10 (not_10_out, A1);
  not not_11 (not_11_out, A1);
  not not_12 (not_12_out, M);
  not not_13 (not_13_out, A2);
  not not_14 (not_14_out, M);
  not not_15 (not_15_out, A0);
  not not_16 (not_16_out, M);
  not not_17 (not_17_out, A1);
  not not_18 (not_18_out, A0);
  not not_19 (not_19_out, A2);
  not not_20 (not_20_out, A1);
  not not_21 (not_21_out, A0);
  not not_22 (not_22_out, M);
  not not_23 (not_23_out, A2);
  and and_6 (and_6_out, not_23_out, A1, not_24_out);
  not not_24 (not_24_out, M);
  and and_7 (and_7_out, A2, A0, M);
  and and_8 (and_8_out, A2, A1, M);
  not not_25 (not_25_out, A2);
  and and_9 (and_9_out, not_25_out, not_26_out);
  not not_26 (not_26_out, A1);
  not not_27 (not_27_out, A2);
  not not_28 (not_28_out, A0);
  and and_10 (and_10_out, not_27_out, not_28_out, not_29_out);
  not not_29 (not_29_out, M);
  not not_30 (not_30_out, A1);
  and and_11 (and_11_out, not_30_out, not_31_out);
  not not_31 (not_31_out, A0);
  and and_12 (and_12_out, A1, A0, M);
  and and_13 (and_13_out, A1, not_32_out);
  not not_32 (not_32_out, A0);
  and and_14 (and_14_out, A2, A1);
  not not_33 (not_33_out, A1);
  and and_15 (and_15_out, not_33_out, not_34_out, not_35_out);
  not not_34 (not_34_out, A0);
  not not_35 (not_35_out, M);
  not not_36 (not_36_out, A2);
  and and_16 (and_16_out, not_36_out, A1, A0);
  and and_17 (and_17_out, A1, A0, M);
  not not_37 (not_37_out, A1);
  and and_18 (and_18_out, A2, not_37_out, not_38_out);
  not not_38 (not_38_out, A0);
  not not_39 (not_39_out, A0);
  not not_40 (not_40_out, A1);
  or or_1 (D3, and_1_out, and_2_out, and_3_out, and_4_out, and_5_out);
  and and_19 (and_19_out, not_9_out, not_10_out, A0);
  and and_20 (and_20_out, not_11_out, A0, not_12_out);
  and and_21 (and_21_out, not_13_out, A1, not_14_out);
  and and_22 (and_22_out, A1, not_15_out, not_16_out);
  and and_23 (and_23_out, A2, not_17_out, not_18_out, M);
  and and_24 (and_24_out, A2, A1, A0, M);
  and and_25 (and_25_out, not_19_out, A0);
  and and_26 (and_26_out, A0, M);
  and and_27 (and_27_out, A2, not_20_out, not_21_out, not_22_out);
  and and_28 (and_28_out, A2, A1, M);
  or or_2 (D0, and_6_out, and_7_out, and_8_out);
  or or_3 (MO, and_9_out, and_10_out, and_11_out, and_12_out);
  or or_4 (Ci, and_13_out, and_14_out);
  or or_5 (FL, and_15_out, and_16_out, and_17_out, and_18_out);
  and and_29 (and_29_out, A1, not_39_out, M);
  or or_6 (CInv, and_29_out, and_30_out);
  and and_30 (and_30_out, A2, not_40_out, A0, M);
  or or_7 (D2, and_19_out, and_20_out, and_21_out, and_22_out, and_23_out, and_24_out);
  or or_8 (D1, and_25_out, and_26_out, and_27_out, and_28_out);
endmodule

module SignEx (
  input  [7:0] A,
  input  Thru,
  output [7:0] Y
);

  wire not_1_out;

  not not_1 (not_1_out, Thru);
  Multiplexer #(.width(8), .disabled(0), .enable("false")) multiplexer_1 (
    .in0({8{A[7]}}), .in1(A), .out(Y), .sel(not_1_out));
endmodule

module ALU (
  input  [7:0] A,
  input  [7:0] B,
  input  [3:0] S,
  output [7:0] Y
);

  // Probe on S
  Multiplexer #(.select(2), .disabled(0), .enable("false")) multiplexer_1 (
    .in0(S[0]), .in1(S[1]), .in2(S[2]), .in3(S[3]), .out(Y[4]), .sel({B[4], A[4]}));
  Multiplexer #(.select(2), .disabled(0), .enable("false")) multiplexer_2 (
    .in0(S[0]), .in1(S[1]), .in2(S[2]), .in3(S[3]), .out(Y[5]), .sel({B[5], A[5]}));
  Multiplexer #(.select(2), .disabled(0), .enable("false")) multiplexer_3 (
    .in0(S[0]), .in1(S[1]), .in2(S[2]), .in3(S[3]), .out(Y[6]), .sel({B[6], A[6]}));
  Multiplexer #(.select(2), .disabled(0), .enable("false")) multiplexer_4 (
    .in0(S[0]), .in1(S[1]), .in2(S[2]), .in3(S[3]), .out(Y[7]), .sel({B[7], A[7]}));
  Multiplexer #(.select(2), .disabled(0), .enable("false")) multiplexer_5 (
    .in0(S[0]), .in1(S[1]), .in2(S[2]), .in3(S[3]), .out(Y[0]), .sel({B[0], A[0]}));
  Multiplexer #(.select(2), .disabled(0), .enable("false")) multiplexer_6 (
    .in0(S[0]), .in1(S[1]), .in2(S[2]), .in3(S[3]), .out(Y[1]), .sel({B[1], A[1]}));
  Multiplexer #(.select(2), .disabled(0), .enable("false")) multiplexer_7 (
    .in0(S[0]), .in1(S[1]), .in2(S[2]), .in3(S[3]), .out(Y[2]), .sel({B[2], A[2]}));
  Multiplexer #(.select(2), .disabled(0), .enable("false")) multiplexer_8 (
    .in0(S[0]), .in1(S[1]), .in2(S[2]), .in3(S[3]), .out(Y[3]), .sel({B[3], A[3]}));

  // Notes on the sheet:
  //   F16
  //   F16
endmodule

module ALU4A (
  input  [3:0] B,
  input  [3:0] A,
  input  CIn,
  output COut,
  output [3:0] Y
);

  wire and_1_out, and_2_out, and_3_out, and_4_out, and_5_out, and_6_out, and_7_out, and_8_out, and_9_out,
       and_10_out, and_11_out, and_12_out, and_13_out, and_14_out, or_2_out, or_3_out, or_4_out, xor_1_out,
       xor_2_out, xor_3_out, xor_4_out;

  xor xor_1 (xor_1_out, B[3], A[3]);
  and and_1 (and_1_out, B[3], A[3]);
  xor xor_2 (xor_2_out, B[2], A[2]);
  and and_2 (and_2_out, B[2], A[2]);
  xor xor_3 (xor_3_out, B[1], A[1]);
  and and_3 (and_3_out, B[1], A[1]);
  xor xor_4 (xor_4_out, B[0], A[0]);
  and and_4 (and_4_out, B[0], A[0]);
  and and_5 (and_5_out, xor_1_out, and_2_out);
  and and_6 (and_6_out, xor_1_out, xor_2_out, and_3_out);
  and and_7 (and_7_out, xor_1_out, xor_2_out, xor_3_out, and_4_out);
  and and_8 (and_8_out, xor_1_out, xor_2_out, xor_3_out, xor_4_out, CIn);
  and and_9 (and_9_out, xor_2_out, and_3_out);
  and and_10 (and_10_out, xor_2_out, xor_3_out, and_4_out);
  and and_11 (and_11_out, xor_2_out, xor_3_out, xor_4_out, CIn);
  and and_12 (and_12_out, xor_3_out, and_4_out);
  and and_13 (and_13_out, xor_3_out, xor_4_out, CIn);
  and and_14 (and_14_out, xor_4_out, CIn);
  or or_1 (COut, and_1_out, and_5_out, and_6_out, and_7_out, and_8_out);
  or or_2 (or_2_out, and_2_out, and_9_out, and_10_out, and_11_out);
  or or_3 (or_3_out, and_3_out, and_12_out, and_13_out);
  or or_4 (or_4_out, and_4_out, and_14_out);
  xor xor_5 (Y[3], xor_1_out, or_2_out);
  xor xor_6 (Y[2], xor_2_out, or_3_out);
  xor xor_7 (Y[1], xor_3_out, or_4_out);
  xor xor_8 (Y[0], xor_4_out, CIn);
endmodule

module ALU8A (
  input  [7:0] B,
  input  [7:0] A,
  input  Cin,
  output CY,
  output [7:0] Y
);

  wire alu4a_2_cout;

  ALU4A alu4a_1 (.B(B[7:4]), .A(A[7:4]), .CIn(alu4a_2_cout), .COut(CY), .Y(Y[7:4]));
  ALU4A alu4a_2 (.B(B[3:0]), .A(A[3:0]), .CIn(Cin), .COut(alu4a_2_cout), .Y(Y[3:0]));
endmodule

module ZeroFlag (
  input  [7:0] A,
  output Y
);

  nor nor_1 (Y, A[0], A[1], A[2], A[3], A[4], A[5], A[6], A[7]);
endmodule

module MUX4to1x8 (
  input  [7:0] D0,
  input  [7:0] D1,
  input  [7:0] D2,
  input  [7:0] D3,
  input  [1:0] Sel,
  output [7:0] Y,
  output I0,
  output I1,
  output I2,
  output I3
);

  Multiplexer #(.select(2), .width(8), .enable("false")) multiplexer_1 (
    .in0(D0), .in1(D1), .in2(D2), .in3(D3), .out(Y), .sel(Sel));
  Demultiplexer #(.select(2), .disabled(0), .enable("false")) demultiplexer_1 (
    .out0(I0), .out1(I1), .out2(I2), .out3(I3), .in(1'b1), .sel(Sel));

  // Notes on the sheet:
  //   139
endmodule

module MUX4to1x16 (
  input  [15:0] D0,
  input  [15:0] D1,
  input  [15:0] D2,
  input  [15:0] D3,
  input  [1:0] Sel,
  output [15:0] Y,
  output I0,
  output I1,
  output I2,
  output I3
);

  Multiplexer #(.select(2), .width(16), .enable("false")) multiplexer_1 (
    .in0(D0), .in1(D1), .in2(D2), .in3(D3), .out(Y), .sel(Sel));
  Demultiplexer #(.select(2), .disabled(0), .enable("false")) demultiplexer_1 (
    .out0(I0), .out1(I1), .out2(I2), .out3(I3), .in(1'b1), .sel(Sel));

  // Notes on the sheet:
  //   139
endmodule
